# Fritzing sketch model_3_ir_led (saved by Fritzing 0.9.9b)
breadboards: 1

parts:
  Part1 = Arduino Uno (Rev3)
  LED1 = smd LED [color="White (4500K)" package="1206 [SMD]"]
  LED2 = smd LED [color="White (4500K)" package="1206 [SMD]"]
  R1 = Resistor [tolerance=±5% resistance=10k package="0805 [SMD]"]
  R2 = Resistor [tolerance=±5% resistance=10k package="0805 [SMD]"]
  Part2 = IR Receiver Breakout [package=PCB]
  R3 = Photocell (LDR) [package=THT]
  R4 = Photocell (LDR) [package=THT]
  R5 = Resistor [tolerance=±5% resistance=180 package="1206 [SMD]"]
  R6 = Resistor [tolerance=±5% resistance=180 package="1206 [SMD]"]

nets:
  N1: Part1.A0, R1.Pin_1
  N2: Part1.A3, R2.Pin_1, R4.pin_0
  N3: Part1.D2, Part2.OUT
  N4: Part1.D5_PWM, R5.Pin_1, R6.Pin_1
  5V: Part1.5V, Part2.VCC
  GND: Part1.GND, LED1.cathode, LED2.cathode, Part2.GND, R3.pin_1, R4.pin_1
  N5: LED1.anode, LED2.anode, R5.Pin_0, R6.Pin_0
