# Fritzing sketch model_2_rgb (saved by Fritzing 0.9.6b)
breadboards: 1

parts:
  Part1 = Arduino Uno (Rev3)
  LED1 = RGB LED (com. cathode, rbg) [package="5 mm [THT]"]
  LED2 = RGB LED (com. cathode, rbg) [package="5 mm [THT]"]
  R1 = Resistor [tolerance=±5% resistance=220 package="2512 [SMD]"]
  R2 = Resistor [tolerance=±5% resistance=220 package="2512 [SMD]"]
  R3 = Resistor [tolerance=±5% power=0.25 resistance=330 package=THT]

nets:
  N1: Part1.A1, R3.Pin_0
  N2: Part1.A2, R1.Pin_0
  N3: Part1.A4/SDA, R2.Pin_0
  N4: Part1.GND, LED1.common_cathode, LED2.common_cathode
  N5: LED1.red_anode, LED2.red_anode, R3.Pin_1
  N6: LED1.blue_anode, LED2.blue_anode, R1.Pin_1
  N7: LED1.green_anode, LED2.green_anode, R2.Pin_1
