# Fritzing sketch model_3_ir_led (saved by Fritzing 0.9.6b)
breadboards: 1

parts:
  Part1 = Arduino Uno (Rev3)
  LED1 = smd LED [color="White (4500K)" package="1206 [SMD]"]
  LED2 = smd LED [color="White (4500K)" package="1206 [SMD]"]
  R1 = Resistor [tolerance=±5% resistance=330 package="0805 [SMD]"]
  R2 = Resistor [tolerance=±5% resistance=330 package="0805 [SMD]"]
  Part2 = IR Receiver Breakout [package=PCB]

nets:
  N1: Part1.D2, Part2.OUT
  N2: Part1.D5_PWM, R1.Pin_0, R2.Pin_1
  5V: Part1.5V, Part2.VCC
  GND: Part1.GND, LED1.cathode, LED2.cathode, Part2.GND
  N3: LED1.anode, R1.Pin_1
  N4: LED2.anode, R2.Pin_0
