# Fritzing sketch model_4_pr (saved by Fritzing 0.9.6b)
breadboards: 1

parts:
  R1 = Resistor [tolerance=±5% power=0.25 resistance=10k package=THT]
  R2 = Resistor [tolerance=±5% power=0.25 resistance=10k package=THT]
  Part1 = Arduino Uno (Rev3)
  R3 = PHOTOCELL [package=photocell]
  R4 = PHOTOCELL [package=photocell]

nets:
  N1: R1.Pin_0, Part1.A0, R4.P$2
  N2: R1.Pin_1, R2.Pin_1, Part1.GND, R3.P$2, R4.P$1
  N3: R2.Pin_0, Part1.A4/SDA, R3.P$1
